// Logisim project control_logic.circ as structural Verilog: 1 circuit, main circuit control_logic
module control_logic (
  input  [31:0] inst,
  input  BrEq,
  input  BrLt,
  output PCSel,
  output RegWEn,
  output [2:0] ImmSel,
  output BrUn,
  output ASel,
  output BSel,
  output [3:0] ALUSel,
  output MemRW,
  output [1:0] WBSel,
  output CSRSel,
  output CSRWen
);

  wire ADD, ADDI, and_1_out, and_2_out, and_3_out, and_5_out, and_38_out, and_41_out, and_42_out, and_43_out,
       and_44_out, ANDD, ANDI, AUPIC, B, BEq, BLt, comparator_1_eq, CSR, CSRRC, CSRRCI, CSRRS, CSRRSI, CSRRW,
       CSRRWI, decoder_2_out0, decoder_2_out1, decoder_2_out2, decoder_2_out3, decoder_2_out4,
       decoder_2_out5, decoder_2_out6, decoder_2_out7, decoder_3_out0, decoder_3_out1, decoder_3_out2, DIV,
       DIVU, EBREAK, ECALL, FENCE, I, J, JALR, L, MUL, MULH, MULHSU, MULHU, not_2_out, not_3_out, not_4_out,
       or_1_out, or_2_out, or_3_out, or_4_out, or_5_out, or_6_out, or_7_out, or_8_out, or_9_out, or_10_out,
       or_11_out, or_12_out, or_13_out, ORI, ORR, R, REMM, REMU, SLLI, SLLL, SLT, SLTI, SLTIU, SLTU, SRAA,
       SRAI, SRLI, SRLL, SUB, U, XORI, XORR;

  Decoder #(.select(5)) decoder_1 (
    .out0(L), .out3(FENCE), .out4(I), .out5(AUPIC), .out8(MemRW), .out12(R), .out13(U), .out24(B),
    .out25(JALR), .out27(J), .out28(CSR), .sel(inst[6:2]));  // open: out1, out2, out6, out7, out9, out10, out11, out14, out15, out16, out17, out18, out19, out20, out21, out22, out23, out26, out29, out30, out31, en
  or or_1 (or_1_out, ANDI, ANDD);
  or or_2 (or_2_out, ORI, ORR);
  or or_3 (or_3_out, XORR, XORI);
  or or_4 (or_4_out, SRLL, SRLI);
  and and_1 (and_1_out, B, BEq);
  and and_2 (and_2_out, and_1_out, BrEq);
  and and_3 (and_3_out, B, BLt);
  and and_4 (BrUn, and_3_out, BrLt);
  or or_5 (or_5_out, L, MemRW, J, B, JALR, AUPIC, ADD, ADDI);
  or or_6 (or_6_out, SRAI, SRAA);
  or or_7 (or_7_out, SLLI, SLLL);
  or or_8 (or_8_out, L, MemRW, B);
  or or_9 (or_9_out, R, I, AUPIC);
  or or_10 (or_10_out, J, JALR);
  or or_11 (or_11_out, R, I, L, JALR);
  or or_12 (or_12_out, SLT, SLTU, SLTI, SLTIU);
  or or_13 (or_13_out, MUL, MULHSU);
  or or_14 (RegWEn, R, I, L, J, JALR, AUPIC, CSR);
  or or_15 (ASel, J, AUPIC, B);
  not not_1 (BSel, R);
  Priority_Encoder #(.select(2)) priority_encoder_1 (
    .in0(or_8_out), .in1(or_9_out), .in2(or_10_out), .in3(CSR), .out(WBSel));  // open: gs, en_out, en_in
  Priority_Encoder priority_encoder_2 (
    .in0(or_11_out), .in1(MemRW), .in2(B), .in3(AUPIC), .in4(J), .in5(CSR), .out(ImmSel));  // open: in6, in7, en_in, gs, en_out
  or or_16 (PCSel, and_2_out, BrUn, J, JALR);
  Priority_Encoder #(.select(4)) priority_encoder_3 (
    .in0(or_5_out), .in1(or_1_out), .in2(or_2_out), .in3(or_3_out), .in4(or_4_out), .in5(or_6_out),
    .in6(or_7_out), .in7(or_12_out), .in10(or_13_out), .in11(MULHU), .in12(SUB), .in14(MULH), .in15(CSR),
    .out(ALUSel));  // open: in8, in9, in13, gs, en_out, en_in
  Decoder #(.select(3)) decoder_2 (
    .out0(decoder_2_out0), .out1(decoder_2_out1), .out2(decoder_2_out2), .out3(decoder_2_out3),
    .out4(decoder_2_out4), .out5(decoder_2_out5), .out6(decoder_2_out6), .out7(decoder_2_out7),
    .sel(inst[14:12]));  // open: en
  Decoder #(.select(2)) decoder_3 (
    .out0(decoder_3_out0), .out1(decoder_3_out1), .out2(decoder_3_out2), .sel({inst[30], inst[25]}));  // open: out3, en
  and and_5 (and_5_out, CSR, decoder_2_out0);
  and and_6 (CSRRW, CSR, decoder_2_out1);
  and and_7 (CSRRS, CSR, decoder_2_out2);
  and and_8 (CSRRC, CSR, decoder_2_out3);
  // AND_Gate and_9 has open pins: in0=CSR, in1=decoder_2_out4, out=open
  and and_10 (CSRRWI, CSR, decoder_2_out5);
  and and_11 (CSRRSI, CSR, decoder_2_out6);
  and and_12 (CSRRCI, CSR, decoder_2_out7);
  and and_13 (ADD, decoder_2_out0, decoder_3_out0);
  and and_14 (MUL, decoder_2_out0, decoder_3_out1);
  and and_15 (SUB, decoder_2_out0, decoder_3_out2);
  and and_16 (SLLL, decoder_2_out1, decoder_3_out0);
  and and_17 (MULH, decoder_2_out1, decoder_3_out1);
  and and_18 (SLT, decoder_2_out2, decoder_3_out0);
  and and_19 (MULHSU, decoder_2_out2, decoder_3_out1);
  and and_20 (SLTU, decoder_2_out3, decoder_3_out0);
  and and_21 (MULHU, decoder_2_out3, decoder_3_out1);
  and and_22 (XORR, decoder_2_out4, decoder_3_out0);
  and and_23 (DIV, decoder_2_out4, decoder_3_out1);
  and and_24 (SRLL, decoder_2_out5, decoder_3_out0);
  and and_25 (DIVU, decoder_2_out5, decoder_3_out1);
  and and_26 (SRAA, decoder_2_out5, decoder_3_out2);
  and and_27 (ORR, decoder_2_out6, decoder_3_out0);
  and and_28 (REMM, decoder_2_out6, decoder_3_out1);
  and and_29 (ANDD, decoder_2_out7, decoder_3_out0);
  and and_30 (REMU, decoder_2_out7, decoder_3_out1);
  and and_31 (EBREAK, inst[25], and_5_out);
  not not_2 (not_2_out, inst[25]);
  and and_32 (ECALL, not_2_out, and_5_out);
  or or_17 (CSRSel, CSRRW, CSRRWI);
  not not_3 (not_3_out, comparator_1_eq);
  Comparator #(.width(5)) comparator_1 (.a(inst[19:15]), .b({5{1'b0}}), .eq(comparator_1_eq));  // open: gt, lt
  and and_33 (ADDI, I, decoder_2_out0);
  and and_34 (SLLI, I, decoder_2_out1);
  and and_35 (SLTI, I, decoder_2_out2);
  and and_36 (SLTIU, I, decoder_2_out3);
  and and_37 (XORI, I, decoder_2_out4);
  and and_38 (and_38_out, I, decoder_2_out5);
  and and_39 (ORI, I, decoder_2_out6);
  and and_40 (ANDI, I, decoder_2_out7);
  and and_41 (and_41_out, not_3_out, CSRRS);
  and and_42 (and_42_out, not_3_out, CSRRC);
  and and_43 (and_43_out, not_3_out, CSRRSI);
  and and_44 (and_44_out, not_3_out, CSRRCI);
  or or_18 (BEq, decoder_2_out0, decoder_2_out1);
  or or_19 (BLt, decoder_2_out4, decoder_2_out5, decoder_2_out6, decoder_2_out7);
  not not_4 (not_4_out, inst[30]);
  and and_45 (SRAI, and_38_out, inst[30]);
  and and_46 (SRLI, and_38_out, not_4_out);
  or or_20 (CSRWen, CSRRW, CSRRWI, and_41_out, and_42_out, and_43_out, and_44_out);

  // Other names for the same wires on the sheet: opcode[6:0] = inst[6:0]; funct3[2:0] = inst[14:12];
  //   RS1[4:0] = inst[19:15]; funct7[6:0] = inst[31:25]; S = MemRW

  // Notes on the sheet:
  //   INPUTS to your circuit
  //   DON'T CHANGE THE LOCATIONS OF THE INPUTS AND OUTPUTS!
  //   OUTPUT from your circuit
endmodule
