// Logisim project cpu.circ as structural Verilog: 1 circuit, main circuit cpu
module cpu (
  input  clk,
  input  [31:0] INSTRUCTION,
  input  [31:0] READ_DATA,
  output [31:0] WRITE_ADDRESS,
  output [31:0] PROGRAM_COUNTER,
  output [31:0] ra,
  output [31:0] sp,
  output [31:0] t0,
  output [31:0] t1,
  output [31:0] t2,
  output [31:0] s0,
  output [31:0] s1,
  output [31:0] a0,
  output [31:0] tohost,
  output [3:0] WRITE_ENABLE,
  output [31:0] WRITE_DATA
);

  wire branch_comp_1_breq, branch_comp_1_brlt, control_logic_1_brun, control_logic_1_bsel,
       control_logic_1_csrwen, control_logic_1_memrw, control_logic_1_pcsel, control_logic_1_regwen;
  wire [1:0] control_logic_1_asel, control_logic_1_wbsel;
  wire [2:0] control_logic_1_immsel;
  wire [3:0] control_logic_1_alusel;
  wire [4:0] INST_EX_q_2;
  wire [31:0] adder_1_out, adder_2_out, alu_1_result, imm_gen_1_imm, INST_EX_q, INST_ID_q, INST_MA_q,
       INST_WB_q, multiplexer_1_out, multiplexer_2_out, multiplexer_3_out, multiplexer_4_out, PC_EX_q,
       PC_ID_q, PC_MA_q, regfile_1_read_data_1, regfile_1_read_data_2, register_1_q, RS1_EX_q, RS2_EX_q;

  Multiplexer #(.enable("false"), .width(32)) multiplexer_1 (
    .in0(adder_1_out), .in1(WRITE_ADDRESS), .out(multiplexer_1_out), .sel(control_logic_1_pcsel));
  Register #(.width(32)) PC (.D(multiplexer_1_out), .clk(clk), .Q(PROGRAM_COUNTER));  // open: en, clr
  Adder #(.width(32)) adder_1 (.a(32'h4), .b(PROGRAM_COUNTER), .out(adder_1_out));  // open: cin, cout
  Register #(.width(32)) PC_ID (.D(PROGRAM_COUNTER), .clk(clk), .Q(PC_ID_q));  // open: en, clr
  Register #(.width(32)) INST_ID (.D(INSTRUCTION), .clk(clk), .Q(INST_ID_q));  // open: en, clr
  control_logic control_logic_1 (
    .CSRWen(control_logic_1_csrwen), .PCSel(control_logic_1_pcsel), .RegWEn(control_logic_1_regwen),
    .ImmSel(control_logic_1_immsel), .BrUn(control_logic_1_brun), .ASel(control_logic_1_asel[0]),
    .BSel(control_logic_1_bsel), .ALUSel(control_logic_1_alusel), .MemRW(control_logic_1_memrw),
    .WBSel(control_logic_1_wbsel), .inst(INSTRUCTION), .BrEq(branch_comp_1_breq), .BrLt(branch_comp_1_brlt));  // open: CSRSel
  regfile regfile_1 (
    .rs1(INST_ID_q[19:15]), .rs2(INST_ID_q[24:20]), .rd(INST_WB_q[11:7]), .Write_Data(register_1_q),
    .RegWEn(control_logic_1_regwen), .clk(clk), .ra(ra), .sp(sp), .t0(t0), .t1(t1), .t2(t2), .s0(s0),
    .s1(s1), .a0(a0), .Read_Data_1(regfile_1_read_data_1), .Read_Data_2(regfile_1_read_data_2));
  Register #(.width(32)) PC_EX (.D(PC_ID_q), .clk(clk), .Q(PC_EX_q));  // open: en, clr
  Register #(.width(32)) RS1_EX (.D(regfile_1_read_data_1), .clk(clk), .Q(RS1_EX_q));  // open: en, clr
  Register #(.width(32)) RS2_EX (.D(regfile_1_read_data_2), .clk(clk), .Q(RS2_EX_q));  // open: en, clr
  Register #(.width(32)) INST_EX (
    .D(INSTRUCTION), .clk(clk), .Q({INST_EX_q[31:20], INST_EX_q_2, INST_EX_q[14:0]}));  // open: en, clr
  assign WRITE_ENABLE = {{3{1'b0}}, control_logic_1_memrw};  // Bit_Extender bit_extender_1
  Comparator #(.mode("unsigned"), .width(5)) comparator_1 (
    .a(INST_EX_q_2), .b(INSTRUCTION[11:7]), .eq(control_logic_1_asel[1]));  // open: gt, lt
  branch_comp branch_comp_1 (
    .rs1(RS1_EX_q), .rs2(RS2_EX_q), .BrUn(control_logic_1_brun), .BrEq(branch_comp_1_breq),
    .BrLt(branch_comp_1_brlt));
  imm_gen imm_gen_1 (
    .inst({INST_EX_q[31:20], INST_EX_q_2, INST_EX_q[14:0]}), .ImmSel(control_logic_1_immsel),
    .imm(imm_gen_1_imm));
  Multiplexer #(.enable("false"), .select(2), .width(32)) multiplexer_2 (
    .in0(RS1_EX_q), .in1(PC_EX_q), .in2(register_1_q), .in3(WRITE_ADDRESS), .out(multiplexer_2_out),
    .sel(control_logic_1_asel));
  Multiplexer #(.enable("false"), .width(32)) multiplexer_3 (
    .in0(RS2_EX_q), .in1(imm_gen_1_imm), .out(multiplexer_3_out), .sel(control_logic_1_bsel));
  alu alu_1 (.Result(alu_1_result), .A(multiplexer_2_out), .B(multiplexer_3_out), .ALUSel(control_logic_1_alusel));
  Register #(.width(32)) PC_MA (.D(PC_EX_q), .clk(clk), .Q(PC_MA_q));  // open: en, clr
  Register #(.width(32)) ALU_MA (.D(alu_1_result), .clk(clk), .Q(WRITE_ADDRESS));  // open: en, clr
  Register #(.width(32)) RS2_MA (.D(RS2_EX_q), .clk(clk), .Q(WRITE_DATA));  // open: en, clr
  Register #(.width(32)) INST_MA (
    .D({INST_EX_q[31:20], INST_EX_q_2, INST_EX_q[14:0]}), .clk(clk), .Q(INST_MA_q));  // open: en, clr
  Adder #(.width(32)) adder_2 (.a(32'h4), .b(PC_MA_q), .out(adder_2_out));  // open: cin, cout
  csr csr_1 (
    .CSR_address(INST_EX_q[31:20]), .CSR_din(RS1_EX_q), .CSR_WE(control_logic_1_csrwen), .tohost(tohost));  // open: clk
  Register #(.width(32)) register_1 (.D(multiplexer_4_out), .clk(clk), .Q(register_1_q));  // open: en, clr
  Multiplexer #(.enable("false"), .select(2), .width(32)) multiplexer_4 (
    .in0(READ_DATA), .in1(WRITE_ADDRESS), .in2(adder_2_out), .in3(tohost), .out(multiplexer_4_out),
    .sel(control_logic_1_wbsel));
  Register #(.width(32)) INST_WB (.D(INST_MA_q), .clk(clk), .Q(INST_WB_q));  // open: en, clr

  // Notes on the sheet:
  //   Output to IMEM
  //   IMEM (do **NOT** move this)
  //   Inputs from IMEM
  //   It is OK to move the PC, RegFile, ALU, MEM, Branch Comp, Imm Gen, and Control Logic to wherever is most convenient for you when constructing your CPU, and to delete this text
  //   Inputs/Outputs for testing. Do **NOT** move these.
  //   Outputs To DMEM
  //   DMEM (do **NOT** move this)
  //   Inputs From DMEM
endmodule
