// Logisim project imm_gen.circ as structural Verilog: 1 circuit, main circuit imm_gen
module imm_gen (
  input  [31:0] inst,
  input  [2:0] ImmSel,
  output [31:0] imm
);

  wire [11:0] demultiplexer_1_out3;
  wire [24:0] demultiplexer_1_out1;
  wire [31:0] demultiplexer_1_out0, demultiplexer_1_out2, demultiplexer_1_out4, demultiplexer_1_out5;

  Demultiplexer #(.enable("false"), .select(3), .width(32)) demultiplexer_1 (
    .out0(demultiplexer_1_out0),
    .out1({demultiplexer_1_out0[31:25], demultiplexer_1_out1[24:12], demultiplexer_1_out0[24:20], demultiplexer_1_out1[6:0]}),
    .out2(demultiplexer_1_out2), .out3({imm[31:12], demultiplexer_1_out3}), .out4(demultiplexer_1_out4),
    .out5(demultiplexer_1_out5), .in(inst), .sel(ImmSel));  // open: out6, out7
  assign imm = {{20{demultiplexer_1_out0[31]}}, demultiplexer_1_out0[31:20]};  // Bit_Extender bit_extender_1
  assign imm = {{19{demultiplexer_1_out2[31]}}, {demultiplexer_1_out2[31], demultiplexer_1_out2[7], demultiplexer_1_out2[30:25], demultiplexer_1_out2[11:8], 1'b0}};  // Bit_Extender bit_extender_2
  assign imm = {{11{demultiplexer_1_out4[31]}}, {demultiplexer_1_out4[31], demultiplexer_1_out4[19:12], demultiplexer_1_out4[20], demultiplexer_1_out4[30:21], 1'b0}};  // Bit_Extender bit_extender_3
  assign imm = {{27{demultiplexer_1_out5[19]}}, demultiplexer_1_out5[19:15]};  // Bit_Extender bit_extender_4
  // also tied to GND on the sheet: {imm[0], imm[1], imm[2], imm[3], imm[4], imm[5], imm[6], imm[7], imm[8], imm[9], imm[10], imm[11]}

  // Notes on the sheet:
  //   INPUTS to your circuit
  //   DON'T CHANGE THE LOCATIONS OF THE INPUTS AND OUTPUTS!
  //   OUTPUT from your circuit
endmodule
